# Fritzing sketch bme-280 (saved by Fritzing 0.9.4)
breadboards: 1

parts:
  Part1 = Adafruit BME280
  Mod1 = Raspberry Pi 4B

nets:
  VIN: Part1.VIN, Mod1.3V3
  GND: Part1.GND, Mod1.GND
  N1: Part1.SCK/SCL, Mod1.GPIO3
  N2: Part1.SDO/ADR, Mod1.GPIO2

custom parts:
  Adafruit BME280: Bosch has stepped up their game with their new BME280 sensor, an environmental sensor with temperature, barometric pressure and humidity! This sensor is great for all sorts of weather/environmental sensing and can even be used in both I2C and SPI! This precision sensor from Bosch is the best low-cost sensing solution for measuring humidity with ±3% accuracy, barometric pressure with ±1 hPa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
